// Logisim project TECLADO.circ as structural Verilog: 2 circuits, main circuit main
module main (
  input  A,
  input  F,
  input  K,
  input  P,
  input  U,
  input  Z,
  input  B,
  input  G,
  input  L,
  input  Q,
  input  V,
  input  SPC,
  input  C,
  input  H,
  input  M,
  input  R,
  input  W,
  input  D,
  input  I,
  input  N,
  input  S,
  input  X,
  input  E,
  input  J,
  input  O,
  input  T,
  input  Y,
  output [7:0] out_28
);

  wire clock_1_out;
  wire [6:0] bit_extender_1_out;
  wire [7:0] rom_1_data;

  assign out_28 = A ? {8{1'b0}} : 8'bz;  // Controlled_Buffer controlled_buffer_1
  assign out_28 = B ? 8'h1 : 8'bz;  // Controlled_Buffer controlled_buffer_2
  assign out_28 = C ? 8'h2 : 8'bz;  // Controlled_Buffer controlled_buffer_3
  assign out_28 = D ? 8'h3 : 8'bz;  // Controlled_Buffer controlled_buffer_4
  assign out_28 = E ? 8'h4 : 8'bz;  // Controlled_Buffer controlled_buffer_5
  assign out_28 = F ? 8'h5 : 8'bz;  // Controlled_Buffer controlled_buffer_6
  assign out_28 = G ? 8'h6 : 8'bz;  // Controlled_Buffer controlled_buffer_7
  assign out_28 = H ? 8'h7 : 8'bz;  // Controlled_Buffer controlled_buffer_8
  assign out_28 = I ? 8'h8 : 8'bz;  // Controlled_Buffer controlled_buffer_9
  assign out_28 = J ? 8'h9 : 8'bz;  // Controlled_Buffer controlled_buffer_10
  assign out_28 = K ? 8'ha : 8'bz;  // Controlled_Buffer controlled_buffer_11
  assign out_28 = L ? 8'hb : 8'bz;  // Controlled_Buffer controlled_buffer_12
  assign out_28 = M ? 8'hc : 8'bz;  // Controlled_Buffer controlled_buffer_13
  assign out_28 = N ? 8'hd : 8'bz;  // Controlled_Buffer controlled_buffer_14
  assign out_28 = O ? 8'he : 8'bz;  // Controlled_Buffer controlled_buffer_15
  assign out_28 = P ? 8'hf : 8'bz;  // Controlled_Buffer controlled_buffer_16
  assign out_28 = Q ? 8'h10 : 8'bz;  // Controlled_Buffer controlled_buffer_17
  assign out_28 = R ? 8'h11 : 8'bz;  // Controlled_Buffer controlled_buffer_18
  assign out_28 = S ? 8'h12 : 8'bz;  // Controlled_Buffer controlled_buffer_19
  assign out_28 = T ? 8'h13 : 8'bz;  // Controlled_Buffer controlled_buffer_20
  assign out_28 = U ? 8'h14 : 8'bz;  // Controlled_Buffer controlled_buffer_21
  assign out_28 = V ? 8'h15 : 8'bz;  // Controlled_Buffer controlled_buffer_22
  assign out_28 = W ? 8'h16 : 8'bz;  // Controlled_Buffer controlled_buffer_23
  assign out_28 = X ? 8'h17 : 8'bz;  // Controlled_Buffer controlled_buffer_24
  assign out_28 = Y ? 8'h18 : 8'bz;  // Controlled_Buffer controlled_buffer_25
  ROM #(.misaligned("true")) rom_1 (.addr(out_28), .data(rom_1_data));
  assign out_28 = Z ? 8'h19 : 8'bz;  // Controlled_Buffer controlled_buffer_26
  assign out_28 = SPC ? 8'h1a : 8'bz;  // Controlled_Buffer controlled_buffer_27
  Clock clock_1 (.out(clock_1_out));
  TTY tty_1 (.data(bit_extender_1_out), .clk(clock_1_out));  // open: we, clr
  Bit_Extender #(.out_width(7)) bit_extender_1 (.in(rom_1_data), .out(bit_extender_1_out));

  // Other names for the same wires on the sheet: REF[7:0] = out_28

  // Notes on the sheet:
  //   contents of rom_1 (hex, n*v repeats v):
  //   41 42 43 44 45 46 47 48 49 4a 4b 4c 4d 4e 4f 50 51 52 53 54 55 56 57 58 59 5a 20
endmodule

module circ (
);

  wire A, B, C, D, E, ESPACO, F, G, H, I, J, K, L, M, N, O, P, Q, R, S, T, U, V, W, X, Y, Z;
  wire [7:0] REF;

  main TecInt (
    .A(A), .B(B), .C(C), .D(D), .E(E), .F(F), .G(G), .H(H), .I(I), .J(J), .K(K), .L(L), .M(M), .N(N), .O(O),
    .P(P), .Q(Q), .R(R), .S(S), .T(T), .U(U), .V(V), .W(W), .X(X), .Y(Y), .Z(Z), .SPC(ESPACO), .out_28(REF));
  Button button_1 (.out(Q));
  Button button_2 (.out(A));
  Button button_3 (.out(Z));
  Button button_4 (.out(W));
  Button button_5 (.out(E));
  Button button_6 (.out(S));
  Button button_7 (.out(D));
  Button button_8 (.out(X));
  Button button_9 (.out(C));
  Button button_10 (.out(R));
  Button button_11 (.out(T));
  Button button_12 (.out(F));
  Button button_13 (.out(G));
  Button button_14 (.out(V));
  Button button_15 (.out(B));
  Button button_16 (.out(Y));
  Button button_17 (.out(U));
  Button button_18 (.out(H));
  Button button_19 (.out(J));
  Button button_20 (.out(N));
  Button button_21 (.out(M));
  Button button_22 (.out(ESPACO));
  Button button_23 (.out(I));
  Button button_24 (.out(O));
  Button button_25 (.out(K));
  Button button_26 (.out(L));
  ROM rom_1 (.addr(REF));  // open: data
  Button button_27 (.out(P));

  // Notes on the sheet:
  //   contents of rom_1 (hex, n*v repeats v):
  //   41 42 43 44 45 46 47 48 49 4a 4b 4c 4d 4e 4f 50 51 52 53 54 55 56 57 58 59 5a 20
endmodule
